# Fritzing sketch servos (saved by Fritzing 0.9.6b)
breadboards: 1

parts:
  J3 = Basic Servo
  J1 = Basic Servo
  J4 = Basic Servo
  C1 = Electrolytic Capacitor [capacitance=1000μF voltage=35V package="1010 [SMD, electrolytic]"]
  IC2 = IC, DIP package, 30 pins [chip_label=ESP32]
  J2 = Basic Servo

nets:
  GND: J3.gnd, J1.gnd, J4.gnd, C1.-, IC2.pin29, J2.gnd
  5V: J3.vcc, J1.vcc, J4.vcc, C1.+, IC2.pin30, J2.vcc
  N1: J3.pulse, IC2.pin26
  N2: J1.pulse, IC2.pin28
  N3: J4.pulse, IC2.pin25
  N4: IC2.pin27, J2.pulse
